# Fritzing sketch Rumble Voyage (saved by Fritzing 0.9.8b)
breadboards: 1

parts:
  元件2 = Arduino Uno (Rev3) - ICSP
  R4 = Resistor [tolerance=±5% power=0.25 resistance=220 package=THT]
  Part1 = KY-037 High Sensitivity Sound Detection Module [package="Breakout board"]
  LED4 = LED - 5mm [color="Red (633nm)" current=0.030 package="5 mm [THT]"]
  LED5 = LED - 5mm [color="Red (633nm)" current=0.030 package="5 mm [THT]"]
  R5 = Resistor [tolerance=±5% power=0.25 resistance=220 package=THT]
  LED6 = LED - 5mm [color="Red (633nm)" current=0.030 package="5 mm [THT]"]
  R6 = Resistor [tolerance=±5% power=0.25 resistance=220 package=THT]
  S2 = Square Pushbutton

nets:
  N1: 元件2.A0, Part1.A0
  N2: 元件2.D9_PWM, LED4.anode
  N3: 元件2.D10_PWM/SS, LED5.anode
  N4: 元件2.D11_PWM/MOSI, LED6.anode
  N5: 元件2.D6_PWM, Part1.D0
  N6: 元件2.D7, 元件2.GND, R4.Pin_1, R5.Pin_1, R6.Pin_1, S2.leg0
  N7: 元件2.5V, Part1.+, S2.leg1
  N8: R4.Pin_0, LED4.cathode
  N9: LED5.cathode, R5.Pin_0
  N10: LED6.cathode, R6.Pin_0

custom parts:
  KY-037 High Sensitivity Sound Detection Module: KY-037 high sensitivity sound detection module is an analog/digital sensor that uses a condenser microphone to observe changes in environment noise.
